// Logisim project Lab4.circ as structural Verilog: 1 circuit, main circuit main
module main (
  input  X,
  output A,
  output B
);

  wire clock_1_out, D_Flip_Flop_qn, NAND_2_out, NAND_out;

  nand NAND (NAND_out, A, X);
  nand NAND_2 (NAND_2_out, A, D_Flip_Flop_qn);
  Clock clock_1 (.out(clock_1_out));
  J_K_Flip_Flop J_K_Flip_Flop (.J(NAND_out), .clk(clock_1_out), .K(NAND_out), .Q(A));  // open: Qn, preset, en, reset
  D_Flip_Flop D_Flip_Flop (.clk(clock_1_out), .D(NAND_2_out), .Q(B), .Qn(D_Flip_Flop_qn));  // open: preset, en, reset

  // Notes on the sheet:
  //   CSC 214 Lab 4
  //   Samuel Jentsch
  //   Clock
endmodule
